// Logisim project 22120152.circ as structural Verilog: 1 circuit, main circuit main
module main (
  input  I3,
  input  I2,
  input  I1,
  input  I0
);

  wire and_1_out, and_2_out, and_3_out, and_4_out, and_5_out, and_6_out, and_7_out, and_8_out, and_9_out,
       and_10_out, and_11_out, and_12_out, and_13_out, and_14_out, and_15_out, and_16_out, not_1_out,
       not_2_out, not_3_out, or_1_out, or_2_out, or_3_out, or_4_out, or_5_out, or_6_out, or_7_out;

  not not_1 (not_1_out, I2);
  not not_2 (not_2_out, I1);
  not not_3 (not_3_out, I0);
  and and_1 (and_1_out, not_1_out, not_3_out);
  and and_2 (and_2_out, not_1_out, not_3_out);
  and and_3 (and_3_out, I1, not_3_out);
  and and_4 (and_4_out, not_1_out, I1);
  and and_5 (and_5_out, I1, not_3_out);
  and and_6 (and_6_out, I1, I0);
  and and_7 (and_7_out, I2, not_2_out, I0);
  and and_8 (and_8_out, not_1_out, not_3_out);
  and and_9 (and_9_out, I2, I0);
  and and_10 (and_10_out, I2, not_3_out);
  and and_11 (and_11_out, not_2_out, not_3_out);
  and and_12 (and_12_out, I2, not_2_out);
  and and_13 (and_13_out, not_1_out, I1);
  and and_14 (and_14_out, I2, not_2_out);
  and and_15 (and_15_out, not_2_out, not_3_out);
  or or_1 (or_1_out, not_2_out, I0, I2);
  and and_16 (and_16_out, I1, not_3_out);
  or or_2 (or_2_out, and_2_out, and_3_out);
  or or_3 (or_3_out, I3, and_7_out, and_4_out, and_1_out, and_5_out);
  or or_4 (or_4_out, and_8_out, I1, I3, and_9_out);
  or or_5 (or_5_out, and_13_out, and_16_out, and_14_out, I3);
  or or_6 (or_6_out, and_10_out, and_11_out, and_12_out, I3);
  or or_7 (or_7_out, and_15_out, and_6_out, not_1_out);
  _7_Segment_Display u_7_segment_display_1 (
    .g(or_5_out), .f(or_6_out), .a(or_4_out), .b(or_7_out), .e(or_2_out), .d(or_3_out), .c(or_1_out));  // open: dp

  // Notes on the sheet:
  //   D3
  //   D1
  //   D2
  //   D0
  //   D5
  //   D4
endmodule
