// Logisim project 22120187.circ as structural Verilog: 1 circuit, main circuit main
module main (
  input  I3,
  input  I2,
  input  I1,
  input  I0
);

  wire and_1_out, and_2_out, and_3_out, and_4_out, and_5_out, not_1_out, not_2_out, not_3_out, or_2_out,
       or_3_out, or_4_out, or_5_out, or_6_out, or_7_out, or_8_out, or_9_out, xor_1_out, xor_2_out;

  not not_1 (not_1_out, I2);
  not not_2 (not_2_out, I1);
  not not_3 (not_3_out, I0);
  or or_1 (not_3_out, not_1_out, I1);
  and and_1 (and_1_out, not_2_out, not_3_out);
  and and_2 (and_2_out, I1, not_1_out);
  and and_3 (and_3_out, not_3_out, not_3_out);
  and and_4 (and_4_out, I2, or_2_out);
  or or_2 (or_2_out, not_2_out, not_3_out);
  and and_5 (and_5_out, not_2_out, I0, I2);
  xor xor_1 (xor_1_out, not_2_out, I0);
  xor xor_2 (xor_2_out, not_1_out, I0);
  or or_3 (or_3_out, not_1_out, xor_1_out);
  or or_4 (or_4_out, I1, I3, xor_2_out);
  or or_5 (or_5_out, I3, and_4_out);
  or or_6 (or_6_out, and_1_out, or_5_out);
  or or_7 (or_7_out, or_5_out, and_2_out);
  _7_Segment_Display u_7_segment_display_1 (
    .g(or_7_out), .f(or_6_out), .a(or_4_out), .b(or_3_out), .e(and_3_out), .d(or_8_out), .c(or_9_out));  // open: dp
  or or_8 (or_8_out, I3, and_3_out, and_2_out, and_5_out);
  or or_9 (or_9_out, not_2_out, I0, I2);
endmodule
